// Logisim project control-logic.circ as structural Verilog: 1 circuit, main circuit control_logic
module control_logic (
  input  [31:0] inst,
  input  BrEq,
  input  BrLt,
  output PCSel,
  output RegWEn,
  output [2:0] ImmSel,
  output BrUn,
  output ASel,
  output BSel,
  output [3:0] ALUSel,
  output MemRW,
  output [1:0] WBSel,
  output CSRSel,
  output CSRWen
);

  wire comparator_2_eq, comparator_3_eq, comparator_6_eq, comparator_7_eq, comparator_9_eq, comparator_10_eq,
       comparator_11_eq, comparator_12_eq, I_f, R_f, S_f, SB_f, U_f, UJ_f;
  wire [2:0] adder_1_out, adder_2_out, adder_3_out, funct3, multiplexer_2_out, multiplexer_3_out,
       multiplexer_4_out, multiplexer_5_out, multiplexer_6_out;
  wire [3:0] adder_4_out, ALUSel_R, ALUSel_U, bit_extender_1_out, bit_extender_2_out, multiplexer_7_out,
       multiplexer_8_out;
  wire [6:0] funct7, opcode;
  wire [31:0] shifter_1_out, shifter_2_out;

  BitSelector #(.group(7), .width(32)) bitselector_1 (.in(inst), .out(opcode), .sel(3'b000));
  Shifter #(.shift("lr"), .width(32)) shifter_1 (.in(inst), .\dist (5'b01100), .out(shifter_1_out));
  not not_1 (BSel, R_f);
  BitSelector #(.group(3), .width(32)) bitselector_2 (.in(shifter_1_out), .out(funct3), .sel(4'b0000));
  Multiplexer #(.enable("false"), .select(3), .width(4)) multiplexer_1 (
    .in0(ALUSel_R), .in1(4'b0000), .in4(ALUSel_U), .out(ALUSel), .sel(ImmSel));  // open: in2, in3, in5, in6, in7
  Shifter #(.shift("lr"), .width(32)) shifter_2 (.in(inst), .\dist (5'b11001), .out(shifter_2_out));
  BitSelector #(.group(7), .width(32)) bitselector_3 (.in(shifter_2_out), .out(funct7), .sel(3'b000));
  Comparator #(.mode("unsigned"), .width(7)) comparator_1 (.a(opcode), .b(7'b0110011), .eq(R_f));  // open: gt, lt
  Comparator #(.mode("unsigned"), .width(7)) comparator_2 (
    .a(opcode), .b(7'b0000011), .eq(comparator_2_eq));  // open: gt, lt
  Comparator #(.mode("unsigned"), .width(7)) comparator_3 (
    .a(opcode), .b(7'b0010011), .eq(comparator_3_eq));  // open: gt, lt
  Comparator #(.mode("unsigned"), .width(7)) comparator_4 (.a(opcode), .b(7'b0100011), .eq(S_f));  // open: gt, lt
  Comparator #(.mode("unsigned"), .width(7)) comparator_5 (.a(opcode), .b(7'b1100011), .eq(SB_f));  // open: gt, lt
  Comparator #(.mode("unsigned"), .width(7)) comparator_6 (
    .a(opcode), .b(7'b0010111), .eq(comparator_6_eq));  // open: gt, lt
  Comparator #(.mode("unsigned"), .width(7)) comparator_7 (
    .a(opcode), .b(7'b0110111), .eq(comparator_7_eq));  // open: gt, lt
  Comparator #(.mode("unsigned"), .width(7)) comparator_8 (.a(opcode), .b(7'b1101111), .eq(UJ_f));  // open: gt, lt
  or or_1 (I_f, comparator_2_eq, comparator_3_eq);
  or or_2 (U_f, comparator_6_eq, comparator_7_eq);
  Multiplexer #(.enable("false"), .width(3)) multiplexer_2 (
    .in0(3'b000), .in1(3'b001), .out(multiplexer_2_out), .sel(I_f));
  Multiplexer #(.enable("false"), .width(3)) multiplexer_3 (
    .in0(3'b000), .in1(3'b010), .out(multiplexer_3_out), .sel(S_f));
  Multiplexer #(.enable("false"), .width(3)) multiplexer_4 (
    .in0(3'b000), .in1(3'b011), .out(multiplexer_4_out), .sel(SB_f));
  Multiplexer #(.enable("false"), .width(3)) multiplexer_5 (
    .in0(3'b000), .in1(3'b100), .out(multiplexer_5_out), .sel(U_f));
  Multiplexer #(.enable("false"), .width(3)) multiplexer_6 (
    .in0(3'b000), .in1(3'b101), .out(multiplexer_6_out), .sel(UJ_f));
  Adder #(.width(3)) adder_1 (.a(multiplexer_2_out), .b(multiplexer_3_out), .out(adder_1_out));  // open: cin, cout
  Adder #(.width(3)) adder_2 (.a(multiplexer_4_out), .b(multiplexer_5_out), .out(adder_2_out));  // open: cin, cout
  assign bit_extender_1_out = {{1{1'b0}}, funct3};  // Bit_Extender bit_extender_1
  Adder #(.width(3)) adder_3 (.a(adder_1_out), .b(adder_2_out), .out(adder_3_out));  // open: cin, cout
  Adder #(.width(4)) adder_4 (.a(bit_extender_1_out), .b(4'b1000), .out(adder_4_out));  // open: cin, cout
  Adder #(.width(3)) adder_5 (.a(adder_3_out), .b(multiplexer_6_out), .out(ImmSel));  // open: cin, cout
  Multiplexer #(.enable("false"), .width(4)) multiplexer_7 (
    .in0(4'b1100), .in1(4'b1101), .out(multiplexer_7_out), .sel(comparator_9_eq));
  Comparator #(.width(3)) comparator_9 (.a(funct3), .b(3'b101), .eq(comparator_9_eq));  // open: gt, lt
  Multiplexer #(.enable("false"), .width(4)) multiplexer_8 (
    .in0(multiplexer_7_out), .in1(adder_4_out), .out(multiplexer_8_out), .sel(comparator_10_eq));
  Comparator #(.width(7)) comparator_10 (.a(funct7), .b(7'b0000001), .eq(comparator_10_eq));  // open: gt, lt
  assign bit_extender_2_out = {{1{1'b0}}, funct3};  // Bit_Extender bit_extender_2
  Comparator #(.width(7)) comparator_11 (.a(funct7), .b({7{1'b0}}), .eq(comparator_11_eq));  // open: gt, lt
  Comparator #(.width(7)) comparator_12 (.a(opcode), .b(7'b0110111), .eq(comparator_12_eq));  // open: gt, lt
  Multiplexer #(.enable("false"), .width(4)) multiplexer_9 (
    .in0(multiplexer_8_out), .in1(bit_extender_2_out), .out(ALUSel_R), .sel(comparator_11_eq));
  Multiplexer #(.enable("false"), .width(4)) multiplexer_10 (
    .in0(4'b0000), .in1(4'b1111), .out(ALUSel_U), .sel(comparator_12_eq));

  assign ASel = 1'b0;
  assign PCSel = 1'b0;
  assign RegWEn = 1'b1;
  assign WBSel = 2'b01;

  // Other names for the same wires on the sheet: inst_type[2:0] = ImmSel

  // Notes on the sheet:
  //   INPUTS to your circuit
  //   DON'T CHANGE THE LOCATIONS OF THE INPUTS AND OUTPUTS!
  //   OUTPUT from your circuit
endmodule
